# Fritzing sketch simon (saved by Fritzing 0.9.3b)
breadboards: 2

parts:
  Componente1 = Arduino Nano (Rev3.0)
  S1 = Pushbutton [package="[THT]"]
  S2 = Pushbutton [package="[THT]"]
  S3 = Pushbutton [package="[THT]"]  # not connected
  S4 = Pushbutton [package="[THT]"]  # not connected
  R2 = Resistor [tolerance=±5% resistance=10k package=THT]  # not connected
  R3 = Resistor [tolerance=±5% resistance=10k package=THT]
  R4 = Resistor [tolerance=±5% resistance=10k package=THT]  # not connected
  R5 = Resistor [tolerance=±5% resistance=1k package=THT]  # not connected
  R6 = Resistor [tolerance=±5% resistance=10k package=THT]  # not connected
  LED1 = LED - 5mm [color="Red (633nm)" package="5 mm [THT]"]
  LED2 = LED - 5mm [color="Red (633nm)" package="5 mm [THT]"]
  LED3 = LED - 5mm [color="Red (633nm)" package="5 mm [THT]"]
  LED4 = LED - 5mm [color="Red (633nm)" package="5 mm [THT]"]
  R7 = Resistor [tolerance=±5% resistance=220 package=THT]
  R8 = Resistor [tolerance=±5% resistance=220 package=THT]
  R9 = Resistor [tolerance=±5% resistance=220 package=THT]
  R10 = Resistor [tolerance=±5% resistance=220 package=THT]
  J1 = Piezo Speaker  # not connected

nets:
  N1: Componente1.D4, LED4.anode
  N2: Componente1.D7, LED1.anode
  N3: Componente1.A0, S1.Pin_1, S1.Pin_2
  N4: S2.Pin_3, S2.Pin_4, R3.Pin_0
  N5: LED1.cathode, R7.Pin_1
  N6: LED2.cathode, R8.Pin_1
  N7: LED3.cathode, R9.Pin_1
  N8: LED4.cathode, R10.Pin_1
  N9: R7.Pin_0, R8.Pin_0, R9.Pin_0, R10.Pin_0
